# Fritzing sketch SmartFurby (saved by Fritzing 0.9.4)
breadboards: 1

parts:
  Bauch = Pushbutton [package=THT]
  Rücken = Pushbutton [package=THT]
  Motor_Startpunkt = Pushbutton [package=THT]
  Lichtsensor_Kopf = Photocell (LDR) [package=THT]
  Hauptmotor = DC Motor
  IR-LED_Kopf = LED - 5mm [color="Infrared (940nm)" package="5 mm [THT]"]
  IR-LED_Motor = LED - 5mm [color="Infrared (940nm)" package="5 mm [THT]"]
  Zunge = Pushbutton [package=THT]
  DFPlayer_Mini1 = DFPlayer MINI [package="DIP (Dual Inline) [THT]"]
  Bauteil1 = Adafruit TB6612 DC and Stepper Motor Driver [part_number="Adafruit #2448"]
  U3 = ESP32S-HiLetgo [part_number=ESP32S-HiLetgo]
  R1 = Resistor [tolerance=±5% resistance=100 package=THT]
  R2 = Resistor [tolerance=±5% resistance=47 package=THT]
  Q1 = Basic FET N-Channel [package="TO220 [THT]"]
  R3 = Resistor [tolerance=±5% resistance=10k package=THT]
  R5 = Resistor [tolerance=±5% resistance=68k package=THT]
  TP1 = TP4056 [chip_label=TP4056 package="DIP (Dual Inline) [THT]"]
  U4 = Mystery Part - 2 pins [chip_label=? package=THT]
  U5 = LIPO-1000mAh [package=lipo-1000]
  Kabelloses_Laden = Inductor [package="400 mil [THT]"]
  SP1 = SPEAKER [package=pcb_mount_speaker]
  Power-Switch = Pushbutton [package=THT]
  Bat_R1 = Resistor [tolerance=±5% resistance=100k package=THT]
  Bat_R2 = Resistor [tolerance=±5% resistance=220k package=THT]
  LED1 = LED - 5mm [color="Red (633nm)" package="5 mm [THT]"]
  Rote_Augen = LED - 5mm [color="Red (633nm)" package="5 mm [THT]"]
  R7 = Resistor [tolerance=±5% resistance=22 package=THT]
  Q2 = Basic FET N-Channel [package="TO220 [THT]"]
  R8 = Resistor [tolerance=±5% resistance=10k package=THT]
  IR-Sensor_Motor = LTR-301 [package=ltr-301]
  IR-Sensor_Kopf = TSOP312.., 314.. [package=THT]

nets:
  GND: Bauch.leg0, Rücken.leg0, Motor_Startpunkt.leg0, IR-LED_Motor.cathode, Zunge.leg0, DFPlayer_Mini1.GND#6, Bauteil1.GND, U3.GND, Q1.source, R3.Pin_1, R5.Pin_1, U4.VOUT-, Q2.source, R8.Pin_1, IR-Sensor_Kopf.GND
  N1: Bauch.leg1, U3.GPIO25
  N2: Rücken.leg1, U3.GPIO33
  N3: Motor_Startpunkt.leg1, U3.GPIO32
  N4: Lichtsensor_Kopf.pin_0, U3.GPIO34, R5.Pin_0
  N5: Lichtsensor_Kopf.pin_1, Bauteil1.VCC, U3.3.3, R1.Pin_1, R2.Pin_0, R7.Pin_1, IR-Sensor_Motor.C, IR-Sensor_Kopf.Vs
  N6: Hauptmotor.pin_1, Bauteil1.MOTORA2
  N7: Hauptmotor.pin_2, Bauteil1.MOTORA1
  N8: IR-LED_Kopf.cathode, Q1.drain
  N9: IR-LED_Kopf.anode, R2.Pin_1
  N10: IR-LED_Motor.anode, R1.Pin_0
  N11: Zunge.leg1, U3.GPIO26
  VCC: DFPlayer_Mini1.VCC, Bauteil1.Vmotor, Bauteil1.PWRIN, U3.VIN, Power-Switch.leg0
  N12: DFPlayer_Mini1.RX, U3.GPIO17
  N13: DFPlayer_Mini1.TX, U3.GPIO16
  N14: DFPlayer_Mini1.SPK1, SP1.-
  N15: DFPlayer_Mini1.SPK2, SP1.+
  N16: DFPlayer_Mini1.BUSY, U3.GPIO5
  N17: Bauteil1.AIN1, U3.GPIO12
  N18: Bauteil1.AIN2, U3.GPIO14
  N19: Bauteil1.PWMA, U3.GPIO13
  N20: U3.GPIO35, Bat_R2.Pin_0
  N21: U3.GPIO27, Q1.gate, R3.Pin_0
  N22: U3.GPIO2, Q2.gate, R8.Pin_0
  N23: U3.GPIO18, IR-Sensor_Motor.E
  N24: U3.GPIO19, IR-Sensor_Kopf.Data
  N25: TP1.pin1, Kabelloses_Laden.pin_1
  N26: TP1.pin2, Kabelloses_Laden.pin_0
  N27: TP1.pin3, U4.VIN+
  N28: TP1.pin4, U5.+, Bat_R1.Pin_0, Bat_R2.Pin_1
  N29: TP1.pin5, U5.-, Bat_R1.Pin_1
  N30: TP1.pin6, U4.VIN-
  N31: U4.VOUT+, Power-Switch.leg1
  N32: LED1.cathode, Q2.drain
  N33: LED1.anode, Rote_Augen.cathode
  N34: Rote_Augen.anode, R7.Pin_0

custom parts:
  DFPlayer MINI: MP3 module by DFRobot.com for playing Music from an SD-Card. Supports WAV and MP3 files.
  Adafruit TB6612 DC and Stepper Motor Driver: Spin two DC motors, step one bi-polar or uni-polar stepper, or fire off two solenoids with 1.2A per channel using the TB6612. These are perhaps better known as "the drivers in our assembled Adafruit Motorshield or Motor HAT." We really like these dual H-bridges, so if you want to control motors without a shield or HAT these are easy to include on any solderless breadboard or perma-proto.
  ESP32S-HiLetgo: HiLetgo ESP-WROOM-32 ESP32 ESP-32S Development Board 2.4GHz Dual-Mode WiFi + Bluetooth Dual Cores Microcontroller The ESP32 integrated with Antenna switches, RF Balun, power amplifiers, low-noise amplifiers, filters, and management modules, and the entire solution occupies the least area of PCB. 2.4 GHz Wi-Fi plus Bluetooth dual-mode chip, with TSMC Ultra-low power consumption 40nm technology,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
  TP4056: A DIP stand-in part for whatever IC you want. With 6 pins on a 300mil dual inline package (DIP) footprint.
  Mystery Part - 2 pins: A dummy, proxy, ersatz, stand-in part for whatever you want. With 2 pins on a 100 mil inline pin header footprint.
